// Logisim project disaster_warning_device.circ as structural Verilog: 6 circuits, main circuit DEVICE
module DEVICE (
  input  MODE,
  input  [1:0] R1R0,
  input  [1:0] S1S0,
  input  [1:0] W1W0,
  input  [1:0] L1L0
);

  wire cyclone_1_out_5, decoder_1_out0, decoder_1_out1, decoder_1_out2, decoder_1_out3, earthquake_1_out_5,
       flood_1_out_5, mode_1_out_5, mode_2_out_5, mode_3_out_5, mode_4_out_5, not_1_out, not_2_out,
       priority_encoder_1_gs, tsunami_1_out_5;
  wire [1:0] priority_encoder_1_out;

  flood flood_1 (.in_1(R1R0), .in_2(S1S0), .in_3(W1W0), .in_4(L1L0), .out_5(flood_1_out_5));
  cyclone cyclone_1 (.in_1(R1R0), .in_2(S1S0), .in_3(W1W0), .in_4(L1L0), .out_5(cyclone_1_out_5));
  earthquake earthquake_1 (.in_1(R1R0), .in_2(S1S0), .in_3(W1W0), .in_4(L1L0), .out_5(earthquake_1_out_5));
  tsunami tsunami_1 (.in_1(R1R0), .in_2(S1S0), .in_3(W1W0), .in_4(L1L0), .out_5(tsunami_1_out_5));
  not not_1 (not_1_out, MODE);
  Priority_Encoder #(.select(2)) priority_encoder_1 (
    .in0(flood_1_out_5), .in1(cyclone_1_out_5), .in2(earthquake_1_out_5), .in3(tsunami_1_out_5),
    .out(priority_encoder_1_out), .gs(priority_encoder_1_gs));  // open: en_out, en_in
  not not_2 (not_2_out, priority_encoder_1_gs);
  Decoder #(.select(2)) decoder_1 (
    .out0(decoder_1_out0), .out1(decoder_1_out1), .out2(decoder_1_out2), .out3(decoder_1_out3),
    .sel(priority_encoder_1_out), .en(priority_encoder_1_gs));
  LED SAFE (.in(not_2_out));
  LED DANGER (.in(priority_encoder_1_gs));
  mode mode_1 (.in_1(MODE), .in_2(flood_1_out_5), .in_3(decoder_1_out0), .in_4(not_1_out), .out_5(mode_1_out_5));
  mode mode_2 (.in_1(MODE), .in_2(cyclone_1_out_5), .in_3(decoder_1_out1), .in_4(not_1_out), .out_5(mode_2_out_5));
  mode mode_3 (.in_1(MODE), .in_2(earthquake_1_out_5), .in_3(decoder_1_out2), .in_4(not_1_out), .out_5(mode_3_out_5));
  mode mode_4 (.in_1(MODE), .in_2(tsunami_1_out_5), .in_3(decoder_1_out3), .in_4(not_1_out), .out_5(mode_4_out_5));
  LED FLOOD_2 (.in(mode_1_out_5));
  LED CYCLONE_2 (.in(mode_2_out_5));
  LED EARTHQUAKE_2 (.in(mode_3_out_5));
  LED TSUNAMI_2 (.in(mode_4_out_5));

  // Notes on the sheet:
  //   Rain
  //   MODE 
  //   0
  //   1
  //   Seismic
  //   TYPE
  //   UNIQUE DISASTER
  //   MULTI DISASTER
  //   Wind
  //   Sea Level
  //   INPUT
  //   00
  //   01
  //   10
  //   11
  //   Flood Condition
  //   Cyclone Condition
  //   Earthquake Condition
  //   Tsunami Condition
  //   IMPACT
  //   Low/None
  //   Medium
  //   High
  //   Very High
  //   DISASTER WARNING DEVICE (S1-T19)
  //   Priority Arrangement
  //   One Hot Disaster
  //   Mode Response
endmodule

module flood (
  input  [1:0] in_1,
  input  [1:0] in_2,
  input  [1:0] in_3,
  input  [1:0] in_4,
  output out_5
);

  wire and_1_out, comparator_1_eq, comparator_1_lt, comparator_2_eq, comparator_3_eq, comparator_3_gt,
       comparator_4_eq, comparator_4_gt, or_1_out, or_2_out, or_3_out, or_4_out;

  Comparator #(.width(2)) comparator_1 (.a(in_1), .b(2'b10), .eq(comparator_1_eq), .lt(comparator_1_lt));  // open: gt
  Comparator #(.width(2)) comparator_2 (.a(in_1), .b(2'b11), .eq(comparator_2_eq));  // open: gt, lt
  Comparator #(.width(2)) comparator_3 (.a(in_3), .b(2'b10), .gt(comparator_3_gt), .eq(comparator_3_eq));  // open: lt
  Comparator #(.width(2)) comparator_4 (.a(in_4), .b(2'b10), .gt(comparator_4_gt), .eq(comparator_4_eq));  // open: lt
  or or_1 (or_1_out, comparator_1_lt, comparator_1_eq);
  or or_2 (or_2_out, comparator_3_gt, comparator_3_eq);
  or or_3 (or_3_out, comparator_4_gt, comparator_4_eq);
  or or_4 (or_4_out, or_2_out, or_3_out);
  or or_5 (out_5, comparator_2_eq, and_1_out);
  and and_1 (and_1_out, or_1_out, or_4_out);

  // Notes on the sheet:
  //   Flood Condition
endmodule

module cyclone (
  input  [1:0] in_1,
  input  [1:0] in_2,
  input  [1:0] in_3,
  input  [1:0] in_4,
  output out_5
);

  wire and_1_out, comparator_1_eq, comparator_1_gt, comparator_2_eq, comparator_2_lt, comparator_3_eq,
       comparator_4_eq, comparator_4_gt, or_1_out, or_2_out, or_3_out, or_4_out;

  Comparator #(.width(2)) comparator_1 (.a(in_1), .b(2'b10), .gt(comparator_1_gt), .eq(comparator_1_eq));  // open: lt
  Comparator #(.width(2)) comparator_2 (.a(in_3), .b(2'b10), .eq(comparator_2_eq), .lt(comparator_2_lt));  // open: gt
  Comparator #(.width(2)) comparator_3 (.a(in_3), .b(2'b11), .eq(comparator_3_eq));  // open: gt, lt
  Comparator #(.width(2)) comparator_4 (.a(in_4), .b(2'b10), .gt(comparator_4_gt), .eq(comparator_4_eq));  // open: lt
  or or_1 (or_1_out, comparator_1_gt, comparator_1_eq);
  or or_2 (or_2_out, comparator_2_lt, comparator_2_eq);
  or or_3 (or_3_out, comparator_4_gt, comparator_4_eq);
  or or_4 (or_4_out, or_1_out, or_3_out);
  and and_1 (and_1_out, or_4_out, or_2_out);
  or or_5 (out_5, and_1_out, comparator_3_eq);

  // Notes on the sheet:
  //   Cyclone Condition
endmodule

module earthquake (
  input  [1:0] in_1,
  input  [1:0] in_2,
  input  [1:0] in_3,
  input  [1:0] in_4,
  output out_5
);

  wire comparator_1_eq, comparator_1_lt, comparator_2_eq, or_1_out;

  Comparator #(.width(2)) comparator_1 (.a(in_2), .b(2'b10), .eq(comparator_1_eq), .lt(comparator_1_lt));  // open: gt
  Comparator #(.width(2)) comparator_2 (.a(in_2), .b(2'b11), .eq(comparator_2_eq));  // open: gt, lt
  or or_1 (or_1_out, comparator_1_lt, comparator_1_eq);
  or or_2 (out_5, or_1_out, comparator_2_eq);

  // Notes on the sheet:
  //   Earthquake Condition
endmodule

module tsunami (
  input  [1:0] in_1,
  input  [1:0] in_2,
  input  [1:0] in_3,
  input  [1:0] in_4,
  output out_5
);

  wire comparator_1_eq, comparator_1_lt, comparator_2_eq, comparator_3_eq, comparator_3_lt, comparator_4_eq,
       or_1_out, or_2_out, or_3_out;

  Comparator #(.width(2)) comparator_1 (.a(in_2), .b(2'b10), .eq(comparator_1_eq), .lt(comparator_1_lt));  // open: gt
  Comparator #(.width(2)) comparator_2 (.a(in_2), .b(2'b11), .eq(comparator_2_eq));  // open: gt, lt
  Comparator #(.width(2)) comparator_3 (.a(in_4), .b(2'b10), .eq(comparator_3_eq), .lt(comparator_3_lt));  // open: gt
  Comparator #(.width(2)) comparator_4 (.a(in_4), .b(2'b11), .eq(comparator_4_eq));  // open: gt, lt
  or or_1 (or_1_out, comparator_1_lt, comparator_1_eq);
  or or_2 (or_2_out, comparator_3_lt, comparator_3_eq);
  or or_3 (or_3_out, or_1_out, comparator_2_eq);
  or or_4 (or_3_out, or_2_out, comparator_4_eq);
  and and_1 (out_5, or_3_out, or_3_out);

  // Notes on the sheet:
  //   Tsunami Condition
endmodule

module mode (
  input  in_1,
  input  in_2,
  input  in_3,
  input  in_4,
  output out_5
);

  wire and_1_out, and_2_out;

  and and_1 (and_1_out, in_1, in_2);
  and and_2 (and_2_out, in_3, in_4);
  or or_1 (out_5, and_1_out, and_2_out);

  // Notes on the sheet:
  //   Mode Response
endmodule
